// Digital circuit 16-stage-shift.dig as structural Verilog
module _16_stage_shift (
  input  [4:0] char_in,
  input  shift_clk,
  input  display_en,
  input  glbl_rst,
  output [4:0] st0,
  output [4:0] st1,
  output [4:0] st2,
  output [4:0] st3,
  output [4:0] st4,
  output [4:0] st5,
  output [4:0] st6,
  output [4:0] st7,
  output [4:0] st8,
  output [4:0] st9,
  output [4:0] st10,
  output [4:0] st11,
  output [4:0] st12,
  output [4:0] st13,
  output [4:0] st14,
  output [4:0] st15
);

  wire [4:0] multiplexer_1_out, multiplexer_2_out, multiplexer_3_out, multiplexer_4_out, multiplexer_5_out,
       multiplexer_6_out, multiplexer_7_out, multiplexer_8_out, multiplexer_9_out, multiplexer_10_out,
       multiplexer_11_out, multiplexer_12_out, multiplexer_13_out, multiplexer_14_out, multiplexer_15_out,
       multiplexer_16_out;

  Multiplexer #(.Bits(5)) multiplexer_1 (.sel(glbl_rst), .in_0(char_in), .in_1({5{1'b1}}), .out(multiplexer_1_out));
  Multiplexer #(.Bits(5)) multiplexer_2 (.sel(glbl_rst), .in_0(st3), .in_1({5{1'b1}}), .out(multiplexer_2_out));
  Multiplexer #(.Bits(5)) multiplexer_3 (.sel(glbl_rst), .in_0(st7), .in_1({5{1'b1}}), .out(multiplexer_3_out));
  Multiplexer #(.Bits(5)) multiplexer_4 (.sel(glbl_rst), .in_0(st11), .in_1({5{1'b1}}), .out(multiplexer_4_out));
  Register #(.Bits(5)) stage_reg_0 (.D(multiplexer_1_out), .C(shift_clk), .en(display_en), .Q(st0));
  Register #(.Bits(5)) stage_reg_4 (.D(multiplexer_2_out), .C(shift_clk), .en(display_en), .Q(st4));
  Register #(.Bits(5)) stage_reg_8 (.D(multiplexer_3_out), .C(shift_clk), .en(display_en), .Q(st8));
  Register #(.Bits(5)) stage_reg_12 (.D(multiplexer_4_out), .C(shift_clk), .en(display_en), .Q(st12));
  Multiplexer #(.Bits(5)) multiplexer_5 (.sel(glbl_rst), .in_0(st0), .in_1({5{1'b1}}), .out(multiplexer_5_out));
  Multiplexer #(.Bits(5)) multiplexer_6 (.sel(glbl_rst), .in_0(st4), .in_1({5{1'b1}}), .out(multiplexer_6_out));
  Multiplexer #(.Bits(5)) multiplexer_7 (.sel(glbl_rst), .in_0(st8), .in_1({5{1'b1}}), .out(multiplexer_7_out));
  Multiplexer #(.Bits(5)) multiplexer_8 (.sel(glbl_rst), .in_0(st12), .in_1({5{1'b1}}), .out(multiplexer_8_out));
  Register #(.Bits(5)) stage_reg_1 (.D(multiplexer_5_out), .C(shift_clk), .en(display_en), .Q(st1));
  Register #(.Bits(5)) stage_reg_5 (.D(multiplexer_6_out), .C(shift_clk), .en(display_en), .Q(st5));
  Register #(.Bits(5)) stage_reg_9 (.D(multiplexer_7_out), .C(shift_clk), .en(display_en), .Q(st9));
  Register #(.Bits(5)) stage_reg_13 (.D(multiplexer_8_out), .C(shift_clk), .en(display_en), .Q(st13));
  Multiplexer #(.Bits(5)) multiplexer_9 (.sel(glbl_rst), .in_0(st1), .in_1({5{1'b1}}), .out(multiplexer_9_out));
  Multiplexer #(.Bits(5)) multiplexer_10 (.sel(glbl_rst), .in_0(st5), .in_1({5{1'b1}}), .out(multiplexer_10_out));
  Multiplexer #(.Bits(5)) multiplexer_11 (.sel(glbl_rst), .in_0(st9), .in_1({5{1'b1}}), .out(multiplexer_11_out));
  Multiplexer #(.Bits(5)) multiplexer_12 (.sel(glbl_rst), .in_0(st13), .in_1({5{1'b1}}), .out(multiplexer_12_out));
  Register #(.Bits(5)) stage_reg_2 (.D(multiplexer_9_out), .C(shift_clk), .en(display_en), .Q(st2));
  Register #(.Bits(5)) stage_reg_6 (.D(multiplexer_10_out), .C(shift_clk), .en(display_en), .Q(st6));
  Register #(.Bits(5)) stage_reg_10 (.D(multiplexer_11_out), .C(shift_clk), .en(display_en), .Q(st10));
  Register #(.Bits(5)) stage_reg_14 (.D(multiplexer_12_out), .C(shift_clk), .en(display_en), .Q(st14));
  Multiplexer #(.Bits(5)) multiplexer_13 (.sel(glbl_rst), .in_0(st2), .in_1({5{1'b1}}), .out(multiplexer_13_out));
  Multiplexer #(.Bits(5)) multiplexer_14 (.sel(glbl_rst), .in_0(st6), .in_1({5{1'b1}}), .out(multiplexer_14_out));
  Multiplexer #(.Bits(5)) multiplexer_15 (.sel(glbl_rst), .in_0(st10), .in_1({5{1'b1}}), .out(multiplexer_15_out));
  Multiplexer #(.Bits(5)) multiplexer_16 (.sel(glbl_rst), .in_0(st14), .in_1({5{1'b1}}), .out(multiplexer_16_out));
  Register #(.Bits(5)) stage_reg_3 (.D(multiplexer_13_out), .C(shift_clk), .en(display_en), .Q(st3));
  Register #(.Bits(5)) stage_reg_7 (.D(multiplexer_14_out), .C(shift_clk), .en(display_en), .Q(st7));
  Register #(.Bits(5)) stage_reg_11 (.D(multiplexer_15_out), .C(shift_clk), .en(display_en), .Q(st11));
  Register #(.Bits(5)) stage_reg_15 (.D(multiplexer_16_out), .C(shift_clk), .en(display_en), .Q(st15));
endmodule
