// Digital circuit 4-argmax-tree.dig as structural Verilog
module _4_argmax_tree (
  input  [16:0] accum_class_score_0,
  input  [16:0] accum_class_score_1,
  input  [16:0] accum_class_score_2,
  input  [16:0] accum_class_score_3,
  output [1:0] fwin
);

  wire [1:0] trial01_w_id, trial23_w_id;
  wire [16:0] trial01_win, trial23_win;

  single_trial trial01 (
    .A(accum_class_score_0), .B(accum_class_score_1), .id_A(2'b00), .id_B(2'b01), .win(trial01_win),
    .w_id(trial01_w_id));
  single_trial trial23 (
    .A(accum_class_score_2), .B(accum_class_score_3), .id_A(2'b10), .id_B(2'b11), .win(trial23_win),
    .w_id(trial23_w_id));
  single_trial finals (
    .A(trial01_win), .B(trial23_win), .id_A(trial01_w_id), .id_B(trial23_w_id), .w_id(fwin));  // open: win

  // Notes on the sheet:
  //   Tournament Argmax Tree & Class Comparator
  //   This combinational circuit determines the highest-scoring category across four 17-bit parallel channels using a two-tiered binary 
  //   elimination tree. Subtractor units calculate differences ($A - B$) to evaluate wins via their sign bits. Multiplexers route winning 
  //   intermediate scores and matching identity tags forward, ultimately outputting the final 2-bit winning class index.
endmodule
