// Digital circuit 4-channel-IAE.dig as structural Verilog
module _4_channel_IAE (
  input  glbl_loop_clk,
  input  glbl_inference_state,
  input  enable_bit__1bit,
  input  [7:0] WEIGHT_0,
  input  [7:0] WEIGHT_1,
  input  [7:0] WEIGHT_2,
  input  [7:0] WEIGHT_3,
  input  glbl_reset,
  output [16:0] accum_class_score_0,
  output [16:0] accum_class_score_1,
  output [16:0] accum_class_score_2,
  output [16:0] accum_class_score_3
);

  single_channel_IAE IAE_0 (
    .enable_bit__1bit(enable_bit__1bit), .WEIGHT(WEIGHT_0), .glbl_loop_clk(glbl_loop_clk),
    .glbl_inference_state(glbl_inference_state), .glbl_reset(glbl_reset),
    .accum_class_score(accum_class_score_0));
  single_channel_IAE IAE_1 (
    .enable_bit__1bit(enable_bit__1bit), .WEIGHT(WEIGHT_1), .glbl_loop_clk(glbl_loop_clk),
    .glbl_inference_state(glbl_inference_state), .glbl_reset(glbl_reset),
    .accum_class_score(accum_class_score_1));
  single_channel_IAE IAE_2 (
    .enable_bit__1bit(enable_bit__1bit), .WEIGHT(WEIGHT_2), .glbl_loop_clk(glbl_loop_clk),
    .glbl_inference_state(glbl_inference_state), .glbl_reset(glbl_reset),
    .accum_class_score(accum_class_score_2));
  single_channel_IAE IAE_3 (
    .enable_bit__1bit(enable_bit__1bit), .WEIGHT(WEIGHT_3), .glbl_loop_clk(glbl_loop_clk),
    .glbl_inference_state(glbl_inference_state), .glbl_reset(glbl_reset),
    .accum_class_score(accum_class_score_3));

  // Notes on the sheet:
  //   4-Channel Inference Accumulator Engine (IAE)
  //   This master module parallelizes four independent single-channel accumulator engines to score four target classes simultaneously. While each 
  //   channel processes its own 8-bit weight input to maintain distinct running totals, they all share global clock, enable, and inference-state signals. 
  //   This ensures perfectly synchronized, overflow-safe 17-bit class score updates across the entire neural network layer.
endmodule
