// Digital circuit 4bit-PRNG.dig as structural Verilog
module _4bit_PRNG (
  input  clk,
  input  glbl_boot,
  output [1:0] \var 
);

  wire d_ff_1_q, d_ff_2_q, d_ff_3_q, d_ff_4_q, or_3_out, xor_1_out;

  D_FF #(.Default(1)) d_ff_1 (.D(xor_1_out), .C(clk), .Q(d_ff_1_q));  // open: nQ
  or or_1 (\var [0], d_ff_1_q, glbl_boot);
  D_FF #(.Default(1)) d_ff_2 (.D(\var [0]), .C(clk), .Q(d_ff_2_q));  // open: nQ
  D_FF d_ff_3 (.D(\var [1]), .C(clk), .Q(d_ff_3_q));  // open: nQ
  or or_2 (\var [1], d_ff_2_q, glbl_boot);
  xor xor_1 (xor_1_out, d_ff_3_q, or_3_out);
  D_FF #(.Default(1)) d_ff_4 (.D(d_ff_3_q), .C(clk), .Q(d_ff_4_q));  // open: nQ
  or or_3 (or_3_out, d_ff_4_q, glbl_boot);

  // Notes on the sheet:
  //   4-Bit LFSR (2-bit Pseudorandom Number Generator)
  //   A 4-bit Linear Feedback Shift Register (LFSR) with the primitive polynomial x^4 + x^3 + 1 (0b1101).
  //   It's a very simple Pseudo-RNG to get varying 2-bit outputs.
endmodule
