// Digital circuit demux-decoder-8to256.dig as structural Verilog
module demux_decoder_8to256 (
  input  [7:0] word_slot_addr,
  output [63:0] O192_255,
  output [63:0] O128_191,
  output [63:0] O64_127,
  output [63:0] O0_63
);

  Demultiplexer #(.Selector_Bits(8)) demultiplexer_1 (
    .sel(word_slot_addr), .in(1'b1), .out_0(O0_63[0]), .out_1(O0_63[1]), .out_2(O0_63[2]), .out_3(O0_63[3]),
    .out_4(O0_63[4]), .out_5(O0_63[5]), .out_6(O0_63[6]), .out_7(O0_63[7]), .out_8(O0_63[8]),
    .out_9(O0_63[9]), .out_10(O0_63[10]), .out_11(O0_63[11]), .out_12(O0_63[12]), .out_13(O0_63[13]),
    .out_14(O0_63[14]), .out_15(O0_63[15]), .out_16(O0_63[16]), .out_17(O0_63[17]), .out_18(O0_63[18]),
    .out_19(O0_63[19]), .out_20(O0_63[20]), .out_21(O0_63[21]), .out_22(O0_63[22]), .out_23(O0_63[23]),
    .out_24(O0_63[24]), .out_25(O0_63[25]), .out_26(O0_63[26]), .out_27(O0_63[27]), .out_28(O0_63[28]),
    .out_29(O0_63[29]), .out_30(O0_63[30]), .out_31(O0_63[31]), .out_32(O0_63[32]), .out_33(O0_63[33]),
    .out_34(O0_63[34]), .out_35(O0_63[35]), .out_36(O0_63[36]), .out_37(O0_63[37]), .out_38(O0_63[38]),
    .out_39(O0_63[39]), .out_40(O0_63[40]), .out_41(O0_63[41]), .out_42(O0_63[42]), .out_43(O0_63[43]),
    .out_44(O0_63[44]), .out_45(O0_63[45]), .out_46(O0_63[46]), .out_47(O0_63[47]), .out_48(O0_63[48]),
    .out_49(O0_63[49]), .out_50(O0_63[50]), .out_51(O0_63[51]), .out_52(O0_63[52]), .out_53(O0_63[53]),
    .out_54(O0_63[54]), .out_55(O0_63[55]), .out_56(O0_63[56]), .out_57(O0_63[57]), .out_58(O0_63[58]),
    .out_59(O0_63[59]), .out_60(O0_63[60]), .out_61(O0_63[61]), .out_62(O0_63[62]), .out_63(O0_63[63]),
    .out_64(O64_127[0]), .out_65(O64_127[1]), .out_66(O64_127[2]), .out_67(O64_127[3]), .out_68(O64_127[4]),
    .out_69(O64_127[5]), .out_70(O64_127[6]), .out_71(O64_127[7]), .out_72(O64_127[8]), .out_73(O64_127[9]),
    .out_74(O64_127[10]), .out_75(O64_127[11]), .out_76(O64_127[12]), .out_77(O64_127[13]),
    .out_78(O64_127[14]), .out_79(O64_127[15]), .out_80(O64_127[16]), .out_81(O64_127[17]),
    .out_82(O64_127[18]), .out_83(O64_127[19]), .out_84(O64_127[20]), .out_85(O64_127[21]),
    .out_86(O64_127[22]), .out_87(O64_127[23]), .out_88(O64_127[24]), .out_89(O64_127[25]),
    .out_90(O64_127[26]), .out_91(O64_127[27]), .out_92(O64_127[28]), .out_93(O64_127[29]),
    .out_94(O64_127[30]), .out_95(O64_127[31]), .out_96(O64_127[32]), .out_97(O64_127[33]),
    .out_98(O64_127[34]), .out_99(O64_127[35]), .out_100(O64_127[36]), .out_101(O64_127[37]),
    .out_102(O64_127[38]), .out_103(O64_127[39]), .out_104(O64_127[40]), .out_105(O64_127[41]),
    .out_106(O64_127[42]), .out_107(O64_127[43]), .out_108(O64_127[44]), .out_109(O64_127[45]),
    .out_110(O64_127[46]), .out_111(O64_127[47]), .out_112(O64_127[48]), .out_113(O64_127[49]),
    .out_114(O64_127[50]), .out_115(O64_127[51]), .out_116(O64_127[52]), .out_117(O64_127[53]),
    .out_118(O64_127[54]), .out_119(O64_127[55]), .out_120(O64_127[56]), .out_121(O64_127[57]),
    .out_122(O64_127[58]), .out_123(O64_127[59]), .out_124(O64_127[60]), .out_125(O64_127[61]),
    .out_126(O64_127[62]), .out_127(O64_127[63]), .out_128(O128_191[0]), .out_129(O128_191[1]),
    .out_130(O128_191[2]), .out_131(O128_191[3]), .out_132(O128_191[4]), .out_133(O128_191[5]),
    .out_134(O128_191[6]), .out_135(O128_191[7]), .out_136(O128_191[8]), .out_137(O128_191[9]),
    .out_138(O128_191[10]), .out_139(O128_191[11]), .out_140(O128_191[12]), .out_141(O128_191[13]),
    .out_142(O128_191[14]), .out_143(O128_191[15]), .out_144(O128_191[16]), .out_145(O128_191[17]),
    .out_146(O128_191[18]), .out_147(O128_191[19]), .out_148(O128_191[20]), .out_149(O128_191[21]),
    .out_150(O128_191[22]), .out_151(O128_191[23]), .out_152(O128_191[24]), .out_153(O128_191[25]),
    .out_154(O128_191[26]), .out_155(O128_191[27]), .out_156(O128_191[28]), .out_157(O128_191[29]),
    .out_158(O128_191[30]), .out_159(O128_191[31]), .out_160(O128_191[32]), .out_161(O128_191[33]),
    .out_162(O128_191[34]), .out_163(O128_191[35]), .out_164(O128_191[36]), .out_165(O128_191[37]),
    .out_166(O128_191[38]), .out_167(O128_191[39]), .out_168(O128_191[40]), .out_169(O128_191[41]),
    .out_170(O128_191[42]), .out_171(O128_191[43]), .out_172(O128_191[44]), .out_173(O128_191[45]),
    .out_174(O128_191[46]), .out_175(O128_191[47]), .out_176(O128_191[48]), .out_177(O128_191[49]),
    .out_178(O128_191[50]), .out_179(O128_191[51]), .out_180(O128_191[52]), .out_181(O128_191[53]),
    .out_182(O128_191[54]), .out_183(O128_191[55]), .out_184(O128_191[56]), .out_185(O128_191[57]),
    .out_186(O128_191[58]), .out_187(O128_191[59]), .out_188(O128_191[60]), .out_189(O128_191[61]),
    .out_190(O128_191[62]), .out_191(O128_191[63]), .out_192(O192_255[0]), .out_193(O192_255[1]),
    .out_194(O192_255[2]), .out_195(O192_255[3]), .out_196(O192_255[4]), .out_197(O192_255[5]),
    .out_198(O192_255[6]), .out_199(O192_255[7]), .out_200(O192_255[8]), .out_201(O192_255[9]),
    .out_202(O192_255[10]), .out_203(O192_255[11]), .out_204(O192_255[12]), .out_205(O192_255[13]),
    .out_206(O192_255[14]), .out_207(O192_255[15]), .out_208(O192_255[16]), .out_209(O192_255[17]),
    .out_210(O192_255[18]), .out_211(O192_255[19]), .out_212(O192_255[20]), .out_213(O192_255[21]),
    .out_214(O192_255[22]), .out_215(O192_255[23]), .out_216(O192_255[24]), .out_217(O192_255[25]),
    .out_218(O192_255[26]), .out_219(O192_255[27]), .out_220(O192_255[28]), .out_221(O192_255[29]),
    .out_222(O192_255[30]), .out_223(O192_255[31]), .out_224(O192_255[32]), .out_225(O192_255[33]),
    .out_226(O192_255[34]), .out_227(O192_255[35]), .out_228(O192_255[36]), .out_229(O192_255[37]),
    .out_230(O192_255[38]), .out_231(O192_255[39]), .out_232(O192_255[40]), .out_233(O192_255[41]),
    .out_234(O192_255[42]), .out_235(O192_255[43]), .out_236(O192_255[44]), .out_237(O192_255[45]),
    .out_238(O192_255[46]), .out_239(O192_255[47]), .out_240(O192_255[48]), .out_241(O192_255[49]),
    .out_242(O192_255[50]), .out_243(O192_255[51]), .out_244(O192_255[52]), .out_245(O192_255[53]),
    .out_246(O192_255[54]), .out_247(O192_255[55]), .out_248(O192_255[56]), .out_249(O192_255[57]),
    .out_250(O192_255[58]), .out_251(O192_255[59]), .out_252(O192_255[60]), .out_253(O192_255[61]),
    .out_254(O192_255[62]), .out_255(O192_255[63]));

  // Notes on the sheet:
  //   Demux Decoder 8 to 256
  //   This module acts as the OneHotDecoder8 from the emulator code. It interprets the 8-bit hash value and converts it into a single active 
  //   line out of 256. As Digital allows only up to 64 bits per splitter/merger input/output pin, I had to divide the 256 bit output into 4 
  //   outputs, each merged by a 64 bit merger. In Minecraft, this will be more cleanly implemented as an 8to256 mux directly
  //   outputting a 1 bit signal for the selected address.
endmodule
