// Digital circuit full-model.dig as structural Verilog
module full_model (
  input  glbl_rst,
  input  SYS_BOOT,
  input  master_clock,
  input  [4:0] char_in,
  input  char_valid,
  input  print_done,
  input  SEND,
  output [4:0] char_stream_out,
  output shift_clk,
  output en_print
);

  wire keyboard_buffer_1_hash_char_strobe, keyboard_buffer_1_punct_excl, keyboard_buffer_1_punct_long,
       keyboard_buffer_1_punct_q, keyboard_buffer_1_word_flush, presence_bit_sel_1_feat_present,
       universal_controller_1_argmax_fin, universal_controller_1_clk_lfsr, universal_controller_1_clk_loop,
       universal_controller_1_inference_en;
  wire [1:0] _4_argmax_tree_1_fwin;
  wire [2:0] token_presence_1_punct_presence;
  wire [4:0] keyboard_buffer_1_hash_char_out;
  wire [7:0] full_weight_rom_1_class0_weight, full_weight_rom_1_class1_weight,
       full_weight_rom_1_class2_weight, full_weight_rom_1_class3_weight, multiplexer_1_out,
       multiplexer_2_out, multiplexer_3_out, multiplexer_4_out, token_hasher_1_word_hash_addr;
  wire [8:0] universal_controller_1_loop_cnt_addr;
  wire [16:0] _4_channel_iae_1_accum_class_score_0, _4_channel_iae_1_accum_class_score_1,
       _4_channel_iae_1_accum_class_score_2, _4_channel_iae_1_accum_class_score_3;
  wire [63:0] token_presence_1_word_presence_0_63, token_presence_1_word_presence_64_127,
       token_presence_1_word_presence_128_191, token_presence_1_word_presence_192_255;

  keyboard_buffer keyboard_buffer_1 (
    .char_in(char_in), .char_valid(char_valid), .glbl_rst(glbl_rst), .SEND_BTN(SEND),
    .hash_char_out(keyboard_buffer_1_hash_char_out), .hash_char_strobe(keyboard_buffer_1_hash_char_strobe),
    .word_flush(keyboard_buffer_1_word_flush), .punct_q(keyboard_buffer_1_punct_q),
    .punct_excl(keyboard_buffer_1_punct_excl), .punct_long(keyboard_buffer_1_punct_long));
  token_hasher token_hasher_1 (
    .hash_char_in(keyboard_buffer_1_hash_char_out), .hash_char_strobe(keyboard_buffer_1_hash_char_strobe),
    .word_flush(keyboard_buffer_1_word_flush), .glbl_rst(glbl_rst),
    .word_hash_addr(token_hasher_1_word_hash_addr));
  token_presence token_presence_1 (
    .word_slot_addr(token_hasher_1_word_hash_addr), .word_flush(keyboard_buffer_1_word_flush),
    .punct_q(keyboard_buffer_1_punct_q), .punct_excl(keyboard_buffer_1_punct_excl),
    .punct_long(keyboard_buffer_1_punct_long), .master_sent_rst(glbl_rst),
    .punct_presence(token_presence_1_punct_presence),
    .word_presence_0_63(token_presence_1_word_presence_0_63),
    .word_presence_64_127(token_presence_1_word_presence_64_127),
    .word_presence_128_191(token_presence_1_word_presence_128_191),
    .word_presence_192_255(token_presence_1_word_presence_192_255));
  universal_controller universal_controller_1 (
    .clk_master(master_clock), .SYS_BOOT(SYS_BOOT), .glbl_rst(glbl_rst), .user_submit(SEND),
    .print_done(print_done), .inference_en(universal_controller_1_inference_en),
    .argmax_fin(universal_controller_1_argmax_fin), .run_printer(en_print),
    .loop_cnt_addr(universal_controller_1_loop_cnt_addr), .clk_lfsr(universal_controller_1_clk_lfsr),
    .clk_loop(universal_controller_1_clk_loop), .clk_printer(shift_clk));  // open: glbl_state
  presence_bit_sel presence_bit_sel_1 (
    .loop_cnt_addr(universal_controller_1_loop_cnt_addr),
    .word_pres_0_63(token_presence_1_word_presence_0_63),
    .word_pres_64_127(token_presence_1_word_presence_64_127),
    .word_pres_128_191(token_presence_1_word_presence_128_191),
    .word_pres_192_255(token_presence_1_word_presence_192_255), .punct_pres(token_presence_1_punct_presence),
    .feat_present(presence_bit_sel_1_feat_present));
  full_weight_ROM full_weight_rom_1 (
    .loop_cnt_addr(universal_controller_1_loop_cnt_addr), .class0_weight(full_weight_rom_1_class0_weight),
    .class1_weight(full_weight_rom_1_class1_weight), .class2_weight(full_weight_rom_1_class2_weight),
    .class3_weight(full_weight_rom_1_class3_weight));
  Multiplexer #(.Bits(8)) multiplexer_1 (
    .sel(presence_bit_sel_1_feat_present), .in_0({8{1'b0}}), .in_1(full_weight_rom_1_class0_weight),
    .out(multiplexer_1_out));
  Multiplexer #(.Bits(8)) multiplexer_2 (
    .sel(presence_bit_sel_1_feat_present), .in_0({8{1'b0}}), .in_1(full_weight_rom_1_class1_weight),
    .out(multiplexer_2_out));
  Multiplexer #(.Bits(8)) multiplexer_3 (
    .sel(presence_bit_sel_1_feat_present), .in_0({8{1'b0}}), .in_1(full_weight_rom_1_class2_weight),
    .out(multiplexer_3_out));
  Multiplexer #(.Bits(8)) multiplexer_4 (
    .sel(presence_bit_sel_1_feat_present), .in_0({8{1'b0}}), .in_1(full_weight_rom_1_class3_weight),
    .out(multiplexer_4_out));
  _4_channel_IAE _4_channel_iae_1 (
    .glbl_loop_clk(universal_controller_1_clk_loop),
    .glbl_inference_state(universal_controller_1_inference_en), .enable_bit(presence_bit_sel_1_feat_present),
    .WEIGHT_0(multiplexer_1_out), .WEIGHT_1(multiplexer_2_out), .WEIGHT_2(multiplexer_3_out),
    .WEIGHT_3(multiplexer_4_out), .glbl_reset(glbl_rst),
    .accum_class_score_0(_4_channel_iae_1_accum_class_score_0),
    .accum_class_score_1(_4_channel_iae_1_accum_class_score_1),
    .accum_class_score_2(_4_channel_iae_1_accum_class_score_2),
    .accum_class_score_3(_4_channel_iae_1_accum_class_score_3));
  _4_argmax_tree _4_argmax_tree_1 (
    .accum_class_score_0(_4_channel_iae_1_accum_class_score_0),
    .accum_class_score_1(_4_channel_iae_1_accum_class_score_1),
    .accum_class_score_2(_4_channel_iae_1_accum_class_score_2),
    .accum_class_score_3(_4_channel_iae_1_accum_class_score_3), .fwin(_4_argmax_tree_1_fwin));
  output_gen output_gen_1 (
    .glbl_boot(SYS_BOOT), .w_id(_4_argmax_tree_1_fwin), .argmax_fin(universal_controller_1_argmax_fin),
    .lfsr_clk(universal_controller_1_clk_lfsr), .print_enable(en_print), .stream_clk(shift_clk),
    .char_stream(char_stream_out));

  // Notes on the sheet:
  //   master_clock: Hz: 40
  //   glbl-state (2 bits)
  //   3 states: IDLE(0), INFERENCE(1), 
  //   OUTPUT(2)
  //   class0 (inform)
  //   class1 (question)
  //   class2 (directive)
  //   class3 (commissive)
  //   Circuit design by:
  //   Yiğit İnceçam
endmodule
