// Digital circuit full-weight-ROM.dig as structural Verilog
module full_weight_ROM (
  input  [8:0] loop_cnt_addr,
  output [7:0] class0_weight,
  output [7:0] class1_weight,
  output [7:0] class2_weight,
  output [7:0] class3_weight
);

  weight_bank_8bit_0 weight_bank_8bit_0_1 (.loop_cnt_addr(loop_cnt_addr), .class_weight(class0_weight));
  weight_bank_8bit_1 weight_bank_8bit_1_1 (.loop_cnt_addr(loop_cnt_addr), .class_weight(class1_weight));
  weight_bank_8bit_2 weight_bank_8bit_2_1 (.loop_cnt_addr(loop_cnt_addr), .class_weight(class2_weight));
  weight_bank_8bit_3 weight_bank_8bit_3_1 (.loop_cnt_addr(loop_cnt_addr), .class_weight(class3_weight));

  // Notes on the sheet:
  //   Model Parameter Memory (Weight ROM Banks)
  //   This component acts as the parallel storage warehouse (our barrels) for the neural network. It decodes a single 9-bit 
  //   sequential loop counter address (0 to 258) to simultaneously look up model weights across four independent, 8-bit 
  //   signed channels. Each channel uses paired low and high-nibble ROM blocks, preparing class parameters for 
  //   immediate accumulation.
endmodule
