// Digital circuit keyboard-buffer.dig as structural Verilog
module keyboard_buffer (
  input  [4:0] char_in,
  input  char_valid,
  input  glbl_rst,
  input  SEND_BTN,
  output [4:0] hash_char_out,
  output hash_char_strobe,
  output word_flush,
  output punct_q,
  output punct_excl,
  output punct_long
);

  wire is_space_eq, not_1_out, or_1_out, or_2_out, or_3_out, rs_ff_as_1_q;
  wire [3:0] word_len_out;

  Register #(.Bits(5)) char_reg (.D(char_in), .C(char_valid), .en(1'b1), .Q(hash_char_out));
  Comparator #(.Bits(5)) is_space (.a(hash_char_out), .b(5'b11010), .eq(is_space_eq));  // open: gt, lt
  Comparator #(.Bits(5)) is_q (.a(hash_char_out), .b(5'b11011), .eq(punct_q));  // open: gt, lt
  Comparator #(.Bits(5)) is_excl (.a(hash_char_out), .b(5'b11100), .eq(punct_excl));  // open: gt, lt
  or or_1 (or_1_out, is_space_eq, SEND_BTN);
  Counter #(.Bits(4)) word_len (.en(1'b1), .C(word_flush), .clr(glbl_rst), .out(word_len_out));  // open: ovf
  and and_1 (word_flush, rs_ff_as_1_q, or_1_out);
  or or_2 (or_2_out, is_space_eq, punct_q, punct_excl);
  or or_3 (or_3_out, glbl_rst, word_flush);
  and and_2 (hash_char_strobe, char_valid, not_1_out);
  not not_1 (not_1_out, or_2_out);
  Comparator #(.Bits(4)) bigger_than_8 (.a(word_len_out), .b(4'b1000), .gt(punct_long));  // open: eq, lt
  RS_ff_as rs_ff_as_1 (.R(or_3_out), .S(hash_char_strobe), .Q(rs_ff_as_1_q));  // open: Q_2

  // Notes on the sheet:
  //   Keyboard Buffer & Boundary Detector
  //   This module captures raw 5-bit character inputs from the keyboard interface. It identifies word boundaries via spaces and detects 
  //   special punctuation. Valid letters are immediately streamed to the hashing engine, while boundary markers trigger word-flushing 
  //   and sentence-length tracking to manage front-end text parsing.
  //   DECODING:
  //   0 to 25: a to z
  //   26: space
  //   27: ?
  //   28: !
  //   29,30: unused
  //   31: NULL (used to
  //   be submit)
  //   submit or space
  //   a word is active
  //   flush pulse (word end)
  //   is control input
  //   is letter input
endmodule
