// Digital circuit model-w-i-no-o.dig as structural Verilog
module model_w_i_no_o (
  input  master_clock,
  input  SYS_BOOT,
  input  glbl_rst,
  input  [4:0] KEYBOARD,
  output [4:0] char_addr11,
  output [4:0] char_addr12,
  output [4:0] char_addr13,
  output [4:0] char_addr14,
  output [4:0] char_addr15,
  output [4:0] char_addr10,
  output [4:0] char_addr9,
  output [4:0] char_addr8,
  output [4:0] char_addr7,
  output [4:0] char_addr6,
  output [4:0] char_addr5,
  output [4:0] char_addr4,
  output [4:0] char_addr3,
  output [4:0] char_addr2,
  output [4:0] char_addr1,
  output [4:0] char_addr0
);

  wire END_PRINT_out, full_model_1_en_print, full_model_1_shift_clk, SEND_BTN_out, TAP_KEY_out;
  wire [4:0] full_model_1_char_stream_out;
  wire [6:0] conv_to_ascii_s;

  Button TAP_KEY (.out(TAP_KEY_out));
  Button SEND_BTN (.out(SEND_BTN_out));
  Button END_PRINT (.out(END_PRINT_out));
  full_model full_model_1 (
    .glbl_rst(glbl_rst), .SYS_BOOT(SYS_BOOT), .master_clock(master_clock), .char_in(KEYBOARD),
    .char_valid(TAP_KEY_out), .print_done(END_PRINT_out), .SEND(SEND_BTN_out),
    .char_stream_out(full_model_1_char_stream_out), .shift_clk(full_model_1_shift_clk),
    .en_print(full_model_1_en_print));
  Add #(.Bits(7)) conv_to_ascii (
    .a({2'b00, full_model_1_char_stream_out}), .b(7'b1000001), .c_i(1'b0), .s(conv_to_ascii_s));  // open: c_o
  Terminal terminal_1 (.D(conv_to_ascii_s), .C(full_model_1_shift_clk), .en(full_model_1_en_print));
  _16_stage_shift _16_stage_shift_1 (
    .char_in(full_model_1_char_stream_out), .shift_clk(full_model_1_shift_clk),
    .display_en(full_model_1_en_print), .glbl_rst(glbl_rst), .st0(char_addr0), .st1(char_addr1),
    .st2(char_addr2), .st3(char_addr3), .st4(char_addr4), .st5(char_addr5), .st6(char_addr6),
    .st7(char_addr7), .st8(char_addr8), .st9(char_addr9), .st10(char_addr10), .st11(char_addr11),
    .st12(char_addr12), .st13(char_addr13), .st14(char_addr14), .st15(char_addr15));
  Comparator #(.Bits(5)) is_print_done (.a(char_addr12), .b({5{1'b1}}));  // open: gt, eq, lt

  // Notes on the sheet:
  //   master_clock: Hz: 40
  //   normally a button, change
  //   to input for verilog export
  //   Initially, I implemented 'END-PRINT' to be a signal that
  //   will be sent out when the entire 16 char response has
  //   completed printing. Then I realized we might want to 
  //   see the response more than once. To allow this, the
  //   signal that triggers the pipeline to go back to IDLE/INPUT
  //   is controlled directly by the user.
  //   USER INPUTS
  //   DECODING:
  //   0 to 25: A to Z
  //   26: space
  //   27: ?
  //   28: !
  //   29,30: unused
  //   31: NULL (used to
  //   be submit)
  //   <-------
  //   HOW TO USE:
  //   -Start Simulation by clicking ▶ at the top hotbar.
  //   -Toggle SYS-BOOT on/off.
  //   -Toggle glbl-rst on/off.
  //   -Write the 5-bit value of the first char you want to write to 
  //   KEYBOARD. Press TAP-KEY.
  //   -Write the 5-bit value of the second char you want to write to 
  //   KEYBOARD. Press TAP-KEY.
  //   -(...)
  //   -Write the 5-bit value of the last char you want to write to 
  //   KEYBOARD. Press TAP-KEY.
  //   -Press SEND-BTN.
  //   -Wait for about 6.5 seconds. You will see the 5-bit characters
  //   being streamed out of the 'char-stream-out' pin of 
  //   'full-model'. The terminal will also pop-up and start printing
  //   the response characters generated by the model (only a-z are
  //   printed correctly in the terminal as it reads only ASCII values, unfit
  //   for our encoding).
  //   this is our ML model.
  //   HARDCODED RESPONSES
  //   Class 0 - Inform:
  //   -"noted"
  //   -"i see"
  //   -"understood"
  //   -"boring"
  //   Class 1 - Question:
  //   -"good question"
  //   -"let me think"
  //   -"tell me more"
  //   -"why ask me"
  //   <------------------------
  //   Class 2 - Directive:
  //   -"i will try"
  //   -"certainly"
  //   -"on it"
  //   -"no way"
  //   Class 3 - Commissive:
  //   -"agreed"
  //   -"sounds good"
  //   -"lets do it"
  //   -"i refuse"
  //   this converts 0-25 letters to ascii and
  //   prints them on the built-in terminal.
  //   just for showcasing
  //   CURRENTLY UNUSED (screen logic)
  //   currently unused
  //   If the stream is 13 chars long (the longest
  //   response), the print is done.
endmodule
