// Digital circuit model-w-io.dig as structural Verilog
module model_w_io (
  input  master_clock,
  input  SYS_BOOT,
  input  glbl_rst,
  input  [4:0] KEYBOARD,
  input  TAP_KEY
);

  wire full_model_1_en_print, full_model_1_shift_clk, is_print_done_lt;
  wire [4:0] _16_stage_shift_1_st0, _16_stage_shift_1_st1, _16_stage_shift_1_st2, _16_stage_shift_1_st3,
       _16_stage_shift_1_st4, _16_stage_shift_1_st5, _16_stage_shift_1_st6, _16_stage_shift_1_st7,
       _16_stage_shift_1_st8, _16_stage_shift_1_st9, _16_stage_shift_1_st10, _16_stage_shift_1_st11,
       _16_stage_shift_1_st12, _16_stage_shift_1_st13, _16_stage_shift_1_st14, _16_stage_shift_1_st15,
       full_model_1_char_stream_out;
  wire [15:0] single_char_rom_1__16bit, single_char_rom_2__16bit, single_char_rom_3__16bit,
       single_char_rom_4__16bit, single_char_rom_5__16bit, single_char_rom_6__16bit,
       single_char_rom_7__16bit, single_char_rom_8__16bit, single_char_rom_9__16bit,
       single_char_rom_10__16bit, single_char_rom_11__16bit, single_char_rom_12__16bit,
       single_char_rom_13__16bit, single_char_rom_14__16bit, single_char_rom_15__16bit,
       single_char_rom_16__16bit;

  full_model full_model_1 (
    .glbl_rst(glbl_rst), .SYS_BOOT(SYS_BOOT), .master_clock(master_clock), .char_in(KEYBOARD),
    .char_valid(TAP_KEY), .print_done(is_print_done_lt), .char_stream_out(full_model_1_char_stream_out),
    .shift_clk(full_model_1_shift_clk), .en_print(full_model_1_en_print));  // open: SEND
  _16_stage_shift _16_stage_shift_1 (
    .char_in(full_model_1_char_stream_out), .shift_clk(full_model_1_shift_clk),
    .display_en(full_model_1_en_print), .glbl_rst(glbl_rst), .st0(_16_stage_shift_1_st0),
    .st1(_16_stage_shift_1_st1), .st2(_16_stage_shift_1_st2), .st3(_16_stage_shift_1_st3),
    .st4(_16_stage_shift_1_st4), .st5(_16_stage_shift_1_st5), .st6(_16_stage_shift_1_st6),
    .st7(_16_stage_shift_1_st7), .st8(_16_stage_shift_1_st8), .st9(_16_stage_shift_1_st9),
    .st10(_16_stage_shift_1_st10), .st11(_16_stage_shift_1_st11), .st12(_16_stage_shift_1_st12),
    .st13(_16_stage_shift_1_st13), .st14(_16_stage_shift_1_st14), .st15(_16_stage_shift_1_st15));
  single_char_rom single_char_rom_1 (.addr(_16_stage_shift_1_st0), ._16bit(single_char_rom_1__16bit));
  single_char_rom single_char_rom_2 (.addr(_16_stage_shift_1_st1), ._16bit(single_char_rom_2__16bit));
  single_char_rom single_char_rom_3 (.addr(_16_stage_shift_1_st2), ._16bit(single_char_rom_3__16bit));
  single_char_rom single_char_rom_4 (.addr(_16_stage_shift_1_st3), ._16bit(single_char_rom_4__16bit));
  single_char_rom single_char_rom_5 (.addr(_16_stage_shift_1_st4), ._16bit(single_char_rom_5__16bit));
  single_char_rom single_char_rom_6 (.addr(_16_stage_shift_1_st5), ._16bit(single_char_rom_6__16bit));
  single_char_rom single_char_rom_7 (.addr(_16_stage_shift_1_st6), ._16bit(single_char_rom_7__16bit));
  single_char_rom single_char_rom_8 (.addr(_16_stage_shift_1_st7), ._16bit(single_char_rom_8__16bit));
  single_char_rom single_char_rom_9 (.addr(_16_stage_shift_1_st8), ._16bit(single_char_rom_9__16bit));
  single_char_rom single_char_rom_10 (.addr(_16_stage_shift_1_st9), ._16bit(single_char_rom_10__16bit));
  single_char_rom single_char_rom_11 (.addr(_16_stage_shift_1_st10), ._16bit(single_char_rom_11__16bit));
  single_char_rom single_char_rom_12 (.addr(_16_stage_shift_1_st11), ._16bit(single_char_rom_12__16bit));
  single_char_rom single_char_rom_13 (.addr(_16_stage_shift_1_st12), ._16bit(single_char_rom_13__16bit));
  single_char_rom single_char_rom_14 (.addr(_16_stage_shift_1_st13), ._16bit(single_char_rom_14__16bit));
  single_char_rom single_char_rom_15 (.addr(_16_stage_shift_1_st14), ._16bit(single_char_rom_15__16bit));
  single_char_rom single_char_rom_16 (.addr(_16_stage_shift_1_st15), ._16bit(single_char_rom_16__16bit));
  SixteenSeg sixteenseg_1 (.led(single_char_rom_16__16bit), .dp(1'b0));
  SixteenSeg sixteenseg_2 (.led(single_char_rom_15__16bit), .dp(1'b0));
  Comparator #(.Bits(5)) is_print_done (
    .a(_16_stage_shift_1_st12), .b({5{1'b1}}), .lt(is_print_done_lt));  // open: gt, eq
  SixteenSeg sixteenseg_3 (.led(single_char_rom_14__16bit), .dp(1'b0));
  SixteenSeg sixteenseg_4 (.led(single_char_rom_13__16bit), .dp(1'b0));
  SixteenSeg sixteenseg_5 (.led(single_char_rom_12__16bit), .dp(1'b0));
  SixteenSeg sixteenseg_6 (.led(single_char_rom_11__16bit), .dp(1'b0));
  SixteenSeg sixteenseg_7 (.led(single_char_rom_10__16bit), .dp(1'b0));
  SixteenSeg sixteenseg_8 (.led(single_char_rom_9__16bit), .dp(1'b0));
  SixteenSeg sixteenseg_9 (.led(single_char_rom_8__16bit), .dp(1'b0));
  SixteenSeg sixteenseg_10 (.led(single_char_rom_7__16bit), .dp(1'b0));
  SixteenSeg sixteenseg_11 (.led(single_char_rom_6__16bit), .dp(1'b0));
  SixteenSeg sixteenseg_12 (.led(single_char_rom_5__16bit), .dp(1'b0));
  SixteenSeg sixteenseg_13 (.led(single_char_rom_4__16bit), .dp(1'b0));
  SixteenSeg sixteenseg_14 (.led(single_char_rom_3__16bit), .dp(1'b0));
  SixteenSeg sixteenseg_15 (.led(single_char_rom_2__16bit), .dp(1'b0));
  SixteenSeg sixteenseg_16 (.led(single_char_rom_1__16bit), .dp(1'b0));

  // Notes on the sheet:
  //   master_clock: Hz: 40
  //   normally a button, changed
  //   to input for verilog export
  //   If the stream is 13 chars long (the longest
  //   response), the print is done.
endmodule
