// Digital circuit output-gen.dig as structural Verilog
module output_gen (
  input  glbl_boot,
  input  [1:0] w_id,
  input  argmax_fin,
  input  lfsr_clk,
  input  print_enable,
  input  stream_clk,
  output [4:0] char_stream
);

  wire [1:0] _4bit_prng_1_var;
  wire [3:0] rnd_response_addr_1_rsp_addr;

  _4bit_PRNG _4bit_prng_1 (.clk(lfsr_clk), .glbl_boot(glbl_boot), .\var (_4bit_prng_1_var));
  rnd_response_addr rnd_response_addr_1 (
    .w_id(w_id), .rnd(_4bit_prng_1_var), .argmax_fin(argmax_fin), .rsp_addr(rnd_response_addr_1_rsp_addr));
  stream_response_char stream_response_char_1 (
    .rsp_addr(rnd_response_addr_1_rsp_addr), .stream_clk(stream_clk), .print_enable(print_enable),
    .glbl_boot(glbl_boot), .char_output(char_stream));

  // Notes on the sheet:
  //   HARDCODED RESPONSES
  //   Class 0 - Inform:
  //   -"noted"
  //   -"i see"
  //   -"understood"
  //   -"boring"
  //   Class 1 - Question:
  //   -"good question"
  //   -"let me think"
  //   -"tell me more"
  //   -"why ask me"
  //   Class 2 - Directive:
  //   -"i will try"
  //   -"certainly"
  //   -"on it"
  //   -"no way"
  //   Class 3 - Commissive:
  //   -"agreed"
  //   -"sounds good"
  //   -"lets do it"
  //   -"i refuse"
  //   Generative Output Logic & Text ROM
  //   This module translates classification indices into sequential text streams. A free-running 4-bit LFSR pseudo-randomly selects one of four response variants. When inference stabilizes,
  //    this variant is latched and concatenated with the 2-bit winning class index to form a high-level ROM block address. A synchronous 4-bit counter increments through the block, 
  //   streaming 5-bit character codes sequentially to the external display.
endmodule
