// Digital circuit presence-bit-sel.dig as structural Verilog
module presence_bit_sel (
  input  [8:0] loop_cnt_addr,
  input  [63:0] word_pres_0_63,
  input  [63:0] word_pres_64_127,
  input  [63:0] word_pres_128_191,
  input  [63:0] word_pres_192_255,
  input  [2:0] punct_pres,
  output feat_present
);

  wire multiplexer_1_out, multiplexer_2_out, multiplexer_3_out, multiplexer_4_out, multiplexer_5_out;

  Multiplexer #(.Selector_Bits(6)) multiplexer_1 (
    .sel(loop_cnt_addr[5:0]), .in_0(word_pres_0_63[0]), .in_1(word_pres_0_63[1]), .in_2(word_pres_0_63[2]),
    .in_3(word_pres_0_63[3]), .in_4(word_pres_0_63[4]), .in_5(word_pres_0_63[5]), .in_6(word_pres_0_63[6]),
    .in_7(word_pres_0_63[7]), .in_8(word_pres_0_63[8]), .in_9(word_pres_0_63[9]), .in_10(word_pres_0_63[10]),
    .in_11(word_pres_0_63[11]), .in_12(word_pres_0_63[12]), .in_13(word_pres_0_63[13]),
    .in_14(word_pres_0_63[14]), .in_15(word_pres_0_63[15]), .in_16(word_pres_0_63[16]),
    .in_17(word_pres_0_63[17]), .in_18(word_pres_0_63[18]), .in_19(word_pres_0_63[19]),
    .in_20(word_pres_0_63[20]), .in_21(word_pres_0_63[21]), .in_22(word_pres_0_63[22]),
    .in_23(word_pres_0_63[23]), .in_24(word_pres_0_63[24]), .in_25(word_pres_0_63[25]),
    .in_26(word_pres_0_63[26]), .in_27(word_pres_0_63[27]), .in_28(word_pres_0_63[28]),
    .in_29(word_pres_0_63[29]), .in_30(word_pres_0_63[30]), .in_31(word_pres_0_63[31]),
    .in_32(word_pres_0_63[32]), .in_33(word_pres_0_63[33]), .in_34(word_pres_0_63[34]),
    .in_35(word_pres_0_63[35]), .in_36(word_pres_0_63[36]), .in_37(word_pres_0_63[37]),
    .in_38(word_pres_0_63[38]), .in_39(word_pres_0_63[39]), .in_40(word_pres_0_63[40]),
    .in_41(word_pres_0_63[41]), .in_42(word_pres_0_63[42]), .in_43(word_pres_0_63[43]),
    .in_44(word_pres_0_63[44]), .in_45(word_pres_0_63[45]), .in_46(word_pres_0_63[46]),
    .in_47(word_pres_0_63[47]), .in_48(word_pres_0_63[48]), .in_49(word_pres_0_63[49]),
    .in_50(word_pres_0_63[50]), .in_51(word_pres_0_63[51]), .in_52(word_pres_0_63[52]),
    .in_53(word_pres_0_63[53]), .in_54(word_pres_0_63[54]), .in_55(word_pres_0_63[55]),
    .in_56(word_pres_0_63[56]), .in_57(word_pres_0_63[57]), .in_58(word_pres_0_63[58]),
    .in_59(word_pres_0_63[59]), .in_60(word_pres_0_63[60]), .in_61(word_pres_0_63[61]),
    .in_62(word_pres_0_63[62]), .in_63(word_pres_0_63[63]), .out(multiplexer_1_out));
  Multiplexer #(.Selector_Bits(6)) multiplexer_2 (
    .sel(loop_cnt_addr[5:0]), .in_0(word_pres_64_127[0]), .in_1(word_pres_64_127[1]),
    .in_2(word_pres_64_127[2]), .in_3(word_pres_64_127[3]), .in_4(word_pres_64_127[4]),
    .in_5(word_pres_64_127[5]), .in_6(word_pres_64_127[6]), .in_7(word_pres_64_127[7]),
    .in_8(word_pres_64_127[8]), .in_9(word_pres_64_127[9]), .in_10(word_pres_64_127[10]),
    .in_11(word_pres_64_127[11]), .in_12(word_pres_64_127[12]), .in_13(word_pres_64_127[13]),
    .in_14(word_pres_64_127[14]), .in_15(word_pres_64_127[15]), .in_16(word_pres_64_127[16]),
    .in_17(word_pres_64_127[17]), .in_18(word_pres_64_127[18]), .in_19(word_pres_64_127[19]),
    .in_20(word_pres_64_127[20]), .in_21(word_pres_64_127[21]), .in_22(word_pres_64_127[22]),
    .in_23(word_pres_64_127[23]), .in_24(word_pres_64_127[24]), .in_25(word_pres_64_127[25]),
    .in_26(word_pres_64_127[26]), .in_27(word_pres_64_127[27]), .in_28(word_pres_64_127[28]),
    .in_29(word_pres_64_127[29]), .in_30(word_pres_64_127[30]), .in_31(word_pres_64_127[31]),
    .in_32(word_pres_64_127[32]), .in_33(word_pres_64_127[33]), .in_34(word_pres_64_127[34]),
    .in_35(word_pres_64_127[35]), .in_36(word_pres_64_127[36]), .in_37(word_pres_64_127[37]),
    .in_38(word_pres_64_127[38]), .in_39(word_pres_64_127[39]), .in_40(word_pres_64_127[40]),
    .in_41(word_pres_64_127[41]), .in_42(word_pres_64_127[42]), .in_43(word_pres_64_127[43]),
    .in_44(word_pres_64_127[44]), .in_45(word_pres_64_127[45]), .in_46(word_pres_64_127[46]),
    .in_47(word_pres_64_127[47]), .in_48(word_pres_64_127[48]), .in_49(word_pres_64_127[49]),
    .in_50(word_pres_64_127[50]), .in_51(word_pres_64_127[51]), .in_52(word_pres_64_127[52]),
    .in_53(word_pres_64_127[53]), .in_54(word_pres_64_127[54]), .in_55(word_pres_64_127[55]),
    .in_56(word_pres_64_127[56]), .in_57(word_pres_64_127[57]), .in_58(word_pres_64_127[58]),
    .in_59(word_pres_64_127[59]), .in_60(word_pres_64_127[60]), .in_61(word_pres_64_127[61]),
    .in_62(word_pres_64_127[62]), .in_63(word_pres_64_127[63]), .out(multiplexer_2_out));
  Multiplexer #(.Selector_Bits(2)) multiplexer_3 (
    .sel(loop_cnt_addr[1:0]), .in_0(punct_pres[0]), .in_1(punct_pres[1]), .in_2(punct_pres[2]), .in_3(1'b0),
    .out(multiplexer_3_out));
  Multiplexer #(.Selector_Bits(6)) multiplexer_4 (
    .sel(loop_cnt_addr[5:0]), .in_0(word_pres_128_191[0]), .in_1(word_pres_128_191[1]),
    .in_2(word_pres_128_191[2]), .in_3(word_pres_128_191[3]), .in_4(word_pres_128_191[4]),
    .in_5(word_pres_128_191[5]), .in_6(word_pres_128_191[6]), .in_7(word_pres_128_191[7]),
    .in_8(word_pres_128_191[8]), .in_9(word_pres_128_191[9]), .in_10(word_pres_128_191[10]),
    .in_11(word_pres_128_191[11]), .in_12(word_pres_128_191[12]), .in_13(word_pres_128_191[13]),
    .in_14(word_pres_128_191[14]), .in_15(word_pres_128_191[15]), .in_16(word_pres_128_191[16]),
    .in_17(word_pres_128_191[17]), .in_18(word_pres_128_191[18]), .in_19(word_pres_128_191[19]),
    .in_20(word_pres_128_191[20]), .in_21(word_pres_128_191[21]), .in_22(word_pres_128_191[22]),
    .in_23(word_pres_128_191[23]), .in_24(word_pres_128_191[24]), .in_25(word_pres_128_191[25]),
    .in_26(word_pres_128_191[26]), .in_27(word_pres_128_191[27]), .in_28(word_pres_128_191[28]),
    .in_29(word_pres_128_191[29]), .in_30(word_pres_128_191[30]), .in_31(word_pres_128_191[31]),
    .in_32(word_pres_128_191[32]), .in_33(word_pres_128_191[33]), .in_34(word_pres_128_191[34]),
    .in_35(word_pres_128_191[35]), .in_36(word_pres_128_191[36]), .in_37(word_pres_128_191[37]),
    .in_38(word_pres_128_191[38]), .in_39(word_pres_128_191[39]), .in_40(word_pres_128_191[40]),
    .in_41(word_pres_128_191[41]), .in_42(word_pres_128_191[42]), .in_43(word_pres_128_191[43]),
    .in_44(word_pres_128_191[44]), .in_45(word_pres_128_191[45]), .in_46(word_pres_128_191[46]),
    .in_47(word_pres_128_191[47]), .in_48(word_pres_128_191[48]), .in_49(word_pres_128_191[49]),
    .in_50(word_pres_128_191[50]), .in_51(word_pres_128_191[51]), .in_52(word_pres_128_191[52]),
    .in_53(word_pres_128_191[53]), .in_54(word_pres_128_191[54]), .in_55(word_pres_128_191[55]),
    .in_56(word_pres_128_191[56]), .in_57(word_pres_128_191[57]), .in_58(word_pres_128_191[58]),
    .in_59(word_pres_128_191[59]), .in_60(word_pres_128_191[60]), .in_61(word_pres_128_191[61]),
    .in_62(word_pres_128_191[62]), .in_63(word_pres_128_191[63]), .out(multiplexer_4_out));
  Multiplexer #(.Selector_Bits(6)) multiplexer_5 (
    .sel(loop_cnt_addr[5:0]), .in_0(word_pres_192_255[0]), .in_1(word_pres_192_255[1]),
    .in_2(word_pres_192_255[2]), .in_3(word_pres_192_255[3]), .in_4(word_pres_192_255[4]),
    .in_5(word_pres_192_255[5]), .in_6(word_pres_192_255[6]), .in_7(word_pres_192_255[7]),
    .in_8(word_pres_192_255[8]), .in_9(word_pres_192_255[9]), .in_10(word_pres_192_255[10]),
    .in_11(word_pres_192_255[11]), .in_12(word_pres_192_255[12]), .in_13(word_pres_192_255[13]),
    .in_14(word_pres_192_255[14]), .in_15(word_pres_192_255[15]), .in_16(word_pres_192_255[16]),
    .in_17(word_pres_192_255[17]), .in_18(word_pres_192_255[18]), .in_19(word_pres_192_255[19]),
    .in_20(word_pres_192_255[20]), .in_21(word_pres_192_255[21]), .in_22(word_pres_192_255[22]),
    .in_23(word_pres_192_255[23]), .in_24(word_pres_192_255[24]), .in_25(word_pres_192_255[25]),
    .in_26(word_pres_192_255[26]), .in_27(word_pres_192_255[27]), .in_28(word_pres_192_255[28]),
    .in_29(word_pres_192_255[29]), .in_30(word_pres_192_255[30]), .in_31(word_pres_192_255[31]),
    .in_32(word_pres_192_255[32]), .in_33(word_pres_192_255[33]), .in_34(word_pres_192_255[34]),
    .in_35(word_pres_192_255[35]), .in_36(word_pres_192_255[36]), .in_37(word_pres_192_255[37]),
    .in_38(word_pres_192_255[38]), .in_39(word_pres_192_255[39]), .in_40(word_pres_192_255[40]),
    .in_41(word_pres_192_255[41]), .in_42(word_pres_192_255[42]), .in_43(word_pres_192_255[43]),
    .in_44(word_pres_192_255[44]), .in_45(word_pres_192_255[45]), .in_46(word_pres_192_255[46]),
    .in_47(word_pres_192_255[47]), .in_48(word_pres_192_255[48]), .in_49(word_pres_192_255[49]),
    .in_50(word_pres_192_255[50]), .in_51(word_pres_192_255[51]), .in_52(word_pres_192_255[52]),
    .in_53(word_pres_192_255[53]), .in_54(word_pres_192_255[54]), .in_55(word_pres_192_255[55]),
    .in_56(word_pres_192_255[56]), .in_57(word_pres_192_255[57]), .in_58(word_pres_192_255[58]),
    .in_59(word_pres_192_255[59]), .in_60(word_pres_192_255[60]), .in_61(word_pres_192_255[61]),
    .in_62(word_pres_192_255[62]), .in_63(word_pres_192_255[63]), .out(multiplexer_5_out));
  Multiplexer #(.Selector_Bits(3)) multiplexer_6 (
    .sel(loop_cnt_addr[8:6]), .in_0(multiplexer_1_out), .in_1(multiplexer_2_out), .in_2(multiplexer_4_out),
    .in_3(multiplexer_5_out), .in_4(multiplexer_3_out), .in_5(1'b0), .in_6(1'b0), .in_7(1'b0),
    .out(feat_present));

  // Notes on the sheet:
  //   Presence Bit Selector Network
  //   This module acts as a hierarchical 259-to-1 multiplexer tree that bridges sentence memory with the parameter ROM. By partitioning the 9-bit loop address into an 
  //   upper 3-bit zone routing chunk and a lower bit sub-index, the network dynamically extracts the exact 1-bit presence flag for the active feature slot.
  //   This single-bit output serves as the master enable signal for the downstream inference engines, instantly gating model weights so that only features actively present 
  //   in the scanned sentence contribute to the final mathematical accumulation.
  //   mux-punctuation
endmodule
