// Digital circuit rnd-response-addr.dig as structural Verilog
module rnd_response_addr (
  input  [1:0] w_id,
  input  [1:0] rnd,
  input  argmax_fin,
  output [3:0] rsp_addr
);

  D_FF #(.Bits(2)) d_ff_1 (.D(rnd), .C(argmax_fin), .Q(rsp_addr[1:0]));  // open: nQ

  assign rsp_addr[3:2] = w_id;

  // Notes on the sheet:
  //   The Variant Capture Latch & Address Assembler
  //   Here, I normally used 2 DFFs to take the snapshot of the PRNG,
  //   which caused the initial 0 value to be read from DFF2 on every
  //   restart of the simulation. We now use a single DFF.
  //   takes snapshot of PRNG
endmodule
