// Digital circuit single-channel-IAE.dig as structural Verilog
module single_channel_IAE (
  input  enable_bit__1bit,
  input  [7:0] WEIGHT,
  input  glbl_loop_clk,
  input  glbl_inference_state,
  input  glbl_reset,
  output [16:0] accum_class_score
);

  wire [7:0] and_1_out;
  wire [16:0] _17bit_RCA_s, multiplexer_1_out;

  assign and_1_out = {8{enable_bit__1bit}} & WEIGHT;  // And and_1, 8 bits wide
  Add #(.Bits(17)) _17bit_RCA (
    .a({{10{and_1_out[7]}}, and_1_out[6:0]}), .b(accum_class_score), .c_i(1'b0), .s(_17bit_RCA_s));  // open: c_o
  Register #(.Bits(17)) _17bit_accum__reg (
    .D(multiplexer_1_out), .C(glbl_loop_clk), .en(glbl_inference_state), .Q(accum_class_score));
  Multiplexer #(.Bits(17)) multiplexer_1 (
    .sel(glbl_reset), .in_0(_17bit_RCA_s), .in_1({17{1'b0}}), .out(multiplexer_1_out));

  // Notes on the sheet:
  //   Single-Channel Inference Accumulator Engine (IAE)
  //   This embedded circuit processes a single class score. It uses an 8-bit AND gate to pass or block incoming signed weights based on feature activity. A sign-extension unit expands valid 8-bit weights to 17 bits 
  //   to prevent math overflow. Finally, a 17-bit ripple-carry adder continuously sums these values into a clocked D-flip-flop register.
  //   GATED-WEIGHT (8bits)
  //   sign-bit
  //   sign extend 8->17 bits
endmodule
