// Digital circuit single-char-rom.dig as structural Verilog
module single_char_rom (
  input  [4:0] addr,
  output [15:0] _16bit
);

  ROM #(.AddrBits(5), .Bits(16)) rom1 (.A(addr), .sel(1'b1), .D(_16bit));

  // Notes on the sheet:
  //   contents of rom1 (hex, n*v repeats v):
  //   f3c0,fc51,cf00,fc12,cfc0,c3c0,df40,33c0,cc12,c612,38c,f00,332a
  //   ,3324,ff00,e3c0,ff04,e3c4,ddc0,c012,3f00,309,3315,2d,21c2,cc09
  //   ,0,e400,3300,ffff,ffff,ffff
endmodule
