// Digital circuit single-trial.dig as structural Verilog
module single_trial (
  input  [16:0] A,
  input  [16:0] B,
  input  [1:0] id_A,
  input  [1:0] id_B,
  output [16:0] win,
  output [1:0] w_id
);

  wire not_2_out;
  wire [16:0] _17bit_adder_s, not_1_out;

  assign not_1_out = ~B;  // Not not_1, 17 bits wide
  Add #(.Bits(17)) _17bit_adder (.a(A), .b(not_1_out), .c_i(1'b1), .s(_17bit_adder_s));  // open: c_o
  Multiplexer #(.Bits(17)) multiplexer_1 (.sel(not_2_out), .in_0(B), .in_1(A), .out(win));
  not not_2 (not_2_out, _17bit_adder_s[16]);
  Multiplexer #(.Bits(2)) multiplexer_2 (.sel(not_2_out), .in_0(id_B), .in_1(id_A), .out(w_id));

  // Notes on the sheet:
  //   Single Compare-and-Route Node
  //   The sub-circuit trial node that takes two 17-bit scores (along with their respective tracking index IDs) and outputs the winning score 
  //   and the winning index.
  //   17bit subtractor (A-B)
  //   17bit NOT
  //   complement
  //   +1 for 2's
  //   sign bit
  //   <---
  //   If the Sign Bit is 0, the result is positive (A>=B).
  //   If the Sign Bit is 1, the result is negative (A<=B).
  //   We run this Sign Bit through a NOT gate. This output is 
  //   the win signal (1 means A wins, 0 means B wins).
  //   17bit mux
endmodule
