// Digital circuit sticky-reg-bank-64bit.dig as structural Verilog
module sticky_reg_bank_64bit (
  input  [63:0] dec_word_in,
  input  word_flush,
  input  master_reset,
  output [63:0] presence
);

  wire [63:0] multiplexer_1_out, or_1_out;

  Register #(.Bits(64)) REG_64 (.D(multiplexer_1_out), .C(word_flush), .en(1'b1), .Q(presence));
  assign or_1_out = presence | dec_word_in;  // Or or_1, 64 bits wide
  Multiplexer #(.Bits(64)) multiplexer_1 (
    .sel(master_reset), .in_0(or_1_out), .in_1({64{1'b0}}), .out(multiplexer_1_out));

  // Notes on the sheet:
  //   Had to be implemented at the 64 bit scale instead of the planned 256 due to 
  //   Digital allowing only up to 64 bit merger outputs.
  //   64 bit, 2 input OR
endmodule
