// Digital circuit stream-response-char.dig as structural Verilog
module stream_response_char (
  input  [3:0] rsp_addr,
  input  stream_clk,
  input  print_enable,
  input  glbl_boot,
  output [4:0] char_output
);

  wire and_1_out, or_1_out;
  wire [3:0] _13char_4bitcnt_out;

  or or_1 (or_1_out, glbl_boot, and_1_out);
  Counter #(.Bits(4)) _13char_4bitcnt (
    .en(print_enable), .C(stream_clk), .clr(or_1_out), .out(_13char_4bitcnt_out));  // open: ovf
  ROM #(.AddrBits(8), .Bits(5)) _5bitROM_w_256addr (
    .A({rsp_addr, _13char_4bitcnt_out}), .sel(print_enable), .D(char_output));
  and and_1 (and_1_out, _13char_4bitcnt_out[0], _13char_4bitcnt_out[2], _13char_4bitcnt_out[3]);

  // Notes on the sheet:
  //   Character Sequencer & Text Response ROM
  //   8-bit ROM address map is laid out like this:
  //   >The lower 4 bits (0 to 12) represent the character index (from the counter).
  //   >The upper 4 bits (0 to 15) represent the rsp-addr (the 2-bit winner class combined with the 2-bit random variant).
  //   This means each text phrase starts at a hex address that is a multiple of 16 (0x10).
  //   NOTE: To write hex data, we must assume a character map dictionary (the CHAR TO CODE in the emulator). 
  //   Since a 5-bit bus supports integers up to 31, a standard mapping fits perfectly: a=1, b=2 ... z=26,
  //   Space = 27 (or 0x1B in hex)
  //   But if the existing screen uses a different custom mapping, we'll simply swap these values out for the screen's 
  //   requirements.
  //   longest response is 'good question', which is 13 chars long.
  //   so we reset the counter when it hits 13 (0b1101), making its 
  //   counting interval [0,12]
  //   <----
  //   contents of _5bitROM_w_256addr (hex, n*v repeats v):
  //   d,e,13,4,3,8*1a,1f,1f,1f,8,1a,12,4,4,8*1a,1f,1f,1f,14,d,3,4,11
  //   ,12,13,e,e,3,1a,1a,1a,1f,1f,1f,1,e,11,8,d,6,7*1a,1f,1f,1f,6,e,e
  //   ,3,1a,10,14,4,12,13,8,e,d,1f,1f,1f,b,4,13,1a,c,4,1a,13,7,8,d,a
  //   ,1a,1f,1f,1f,13,4,b,b,1a,c,4,1a,c,e,11,4,1a,1f,1f,1f,16,7,18,1a
  //   ,0,12,a,1a,c,4,1a,1a,1a,1f,1f,1f,8,1a,16,8,b,b,1a,13,11,18,1a,1a,1a
  //   ,1f,1f,1f,2,4,11,13,0,8,d,b,18,4*1a,1f,1f,1f,e,d,1a,8,13,8*1a
  //   ,1f,1f,1f,d,e,1a,16,0,18,7*1a,1f,1f,1f,0,6,11,4,4,3,7*1a,1f,1f,1f
  //   ,12,e,14,d,3,12,1a,6,e,e,3,1a,1a,1f,1f,1f,b,4,13,12,1a,3,e,1a
  //   ,8,13,1a,1a,1a,1f,1f,1f,8,1a,11,4,5,14,12,4,5*1a,1f,1f,1f
endmodule
