// Digital circuit token-hasher.dig as structural Verilog
module token_hasher (
  input  [4:0] hash_char_in,
  input  hash_char_strobe,
  input  word_flush,
  input  glbl_rst,
  output [7:0] word_hash_addr
);

  wire or_1_out;
  wire [7:0] multiplexer_1_out, xor_1_out;

  assign xor_1_out = {3'b000, hash_char_in} ^ {word_hash_addr[0], word_hash_addr[1], word_hash_addr[2], word_hash_addr[3], word_hash_addr[4], word_hash_addr[5], word_hash_addr[6], word_hash_addr[7]};  // XOr xor_1, 8 bits wide
  or or_1 (or_1_out, word_flush, glbl_rst);
  Multiplexer #(.Bits(8)) multiplexer_1 (.sel(or_1_out), .in_0(xor_1_out), .in_1({8{1'b0}}), .out(multiplexer_1_out));
  Register #(.Bits(8)) hash_reg (.D(multiplexer_1_out), .C(hash_char_strobe), .en(1'b1), .Q(word_hash_addr));

  // Notes on the sheet:
  //   Word Token Hashing Unit
  //   This module executes a cyclical shift-XOR algorithm "h_t = ROL_1(h_t-_1) XOR char-code" to map incoming variable-length words 
  //   into unique, repeatable 8-bit numerical keys. When a word completes, it holds this calculated address completely stable for 
  //   downstream memory logging before resetting itself for the next word.
  //   rotated signal
endmodule
