// Digital circuit token-presence.dig as structural Verilog
module token_presence (
  input  [7:0] word_slot_addr,
  input  word_flush,
  input  punct_q,
  input  punct_excl,
  input  punct_long,
  input  master_sent_rst,
  output [2:0] punct_presence,
  output [63:0] word_presence_0_63,
  output [63:0] word_presence_64_127,
  output [63:0] word_presence_128_191,
  output [63:0] word_presence_192_255
);

  wire [63:0] demux_decoder_8to256_1_o0_63, demux_decoder_8to256_1_o64_127, demux_decoder_8to256_1_o128_191,
       demux_decoder_8to256_1_o192_255;

  demux_decoder_8to256 demux_decoder_8to256_1 (
    .word_slot_addr(word_slot_addr), .O192_255(demux_decoder_8to256_1_o192_255),
    .O128_191(demux_decoder_8to256_1_o128_191), .O64_127(demux_decoder_8to256_1_o64_127),
    .O0_63(demux_decoder_8to256_1_o0_63));
  RS_ff_as rs_ff_as_1 (.R(master_sent_rst), .S(punct_q), .Q(punct_presence[0]));  // open: Q_2
  RS_ff_as rs_ff_as_2 (.R(master_sent_rst), .S(punct_excl), .Q(punct_presence[1]));  // open: Q_2
  RS_ff_as rs_ff_as_3 (.R(master_sent_rst), .S(punct_long), .Q(punct_presence[2]));  // open: Q_2
  sticky_reg_bank_64bit bank192_255 (
    .dec_word_in(demux_decoder_8to256_1_o192_255), .word_flush(word_flush), .master_reset(master_sent_rst),
    .presence(word_presence_192_255));
  sticky_reg_bank_64bit bank_128_191 (
    .dec_word_in(demux_decoder_8to256_1_o128_191), .word_flush(word_flush), .master_reset(master_sent_rst),
    .presence(word_presence_128_191));
  sticky_reg_bank_64bit bank64_127 (
    .dec_word_in(demux_decoder_8to256_1_o64_127), .word_flush(word_flush), .master_reset(master_sent_rst),
    .presence(word_presence_64_127));
  sticky_reg_bank_64bit bank0_63 (
    .dec_word_in(demux_decoder_8to256_1_o0_63), .word_flush(word_flush), .master_reset(master_sent_rst),
    .presence(word_presence_0_63));

  // Notes on the sheet:
  //   Feature Mapping Decoder & Presence Latches
  //   Had to be implemented at the 64 bit scale instead of the planned 256 due to 
  //   Digital allowing only up to 64 bit merger outputs.
  //   This component maps input tokens to sentence memory. An 8-bit word slot address 
  //   is continuously decoded into a one-hot representation, which is clocked into four 
  //   parallel 64-bit sticky registers using the word-flush signal. Dedicated unclocked RS 
  //   flip-flops capture structural punctuation flags instantly, maintaining a stable presence 
  //   vector for analysis.
endmodule
