// Digital circuit universal-controller.dig as structural Verilog
module universal_controller (
  input  clk_master,
  input  SYS_BOOT,
  input  glbl_rst,
  input  user_submit,
  input  print_done,
  output [1:0] glbl_state,
  output inference_en,
  output argmax_fin,
  output run_printer,
  output [8:0] loop_cnt_addr,
  output clk_lfsr,
  output clk_loop,
  output clk_printer
);

  wire clk_prescaler_cmpr_eq, is_it_259_eq, not_1_out, not_2_out, or_1_out, or_2_out;
  wire [1:0] multiplexer_1_out, StateLUT_out;
  wire [9:0] clk_prescaler_cnt_out;

  or or_1 (or_1_out, SYS_BOOT, glbl_rst);
  Register #(.Bits(2)) state_tracker (
    .D(multiplexer_1_out), .C(clk_master), .en(1'b1), .Q({argmax_fin, glbl_state[0]}));
  or or_2 (or_2_out, glbl_rst, user_submit);
  Counter #(.Bits(9)) _9bit_loop_counter (
    .en(inference_en), .C(clk_master), .clr(or_2_out), .out(loop_cnt_addr));  // open: ovf
  LookUpTable #(.Bits(2)) StateLUT (
    .in0(glbl_state[0]), .in1(argmax_fin), .in2(user_submit), .in3(is_it_259_eq), .in4(print_done),
    .out(StateLUT_out));
  Counter #(.Bits(10)) clk_prescaler_cnt (
    .en(1'b1), .C(clk_master), .clr(clk_prescaler_cmpr_eq), .out(clk_prescaler_cnt_out));  // open: ovf
  Multiplexer #(.Bits(2)) multiplexer_1 (.sel(or_1_out), .in_0(StateLUT_out), .in_1(2'b00), .out(multiplexer_1_out));
  Comparator #(.Bits(9)) is_it_259 (.a(loop_cnt_addr), .b(9'h103), .eq(is_it_259_eq));  // open: gt, lt
  Comparator #(.Bits(10)) clk_prescaler_cmpr (
    .a(clk_prescaler_cnt_out), .b(10'h14), .eq(clk_prescaler_cmpr_eq));  // open: gt, lt
  not not_1 (not_1_out, argmax_fin);
  and and_1 (inference_en, glbl_state[0], not_1_out);
  and and_2 (clk_printer, run_printer, clk_prescaler_cmpr_eq);
  not not_2 (not_2_out, glbl_state[0]);
  and and_3 (run_printer, not_2_out, argmax_fin);

  assign clk_lfsr = clk_master;
  assign clk_loop = clk_master;
  assign glbl_state[1] = argmax_fin;

  // Notes on the sheet:
  //   clk_master: Hz: 40
  //   SYS_BOOT: open sesame
  //   LOOK UP TABLE CONTENTS
  //   Every cell not explicitly listed below is filled with 0 so that the machine safely defaults back to the IDLE state if something unexpected happens.
  //   Row 0x00 (No high-register inputs active)
  //   Column 0x00 (Address 0x00): 0 (Current state IDLE, stays IDLE)
  //   Column 0x01 (Address 0x01): 1 (Current state INFERENCE, stays INFERENCE)
  //   Column 0x02 (Address 0x02): 2 (Current state OUTPUT, stays OUTPUT)
  //   Row 0x04 (user-submit is High)
  //   Column 0x00 (Address 0x04): 1  <-- CRITICAL: This kicks off the system! Moves IDLE to INFERENCE.
  //   Column 0x01 (Address 0x05): 1 (Stays in INFERENCE)
  //   Column 0x02 (Address 0x06): 2 (Stays in OUTPUT)
  //   Row 0x08 (loop-ovf is High)
  //   Column 0x00 (Address 0x08): 0
  //   Column 0x01 (Address 0x09): 2  <-- CRITICAL: Inference is done! Moves INFERENCE to OUTPUT.
  //   Column 0x02 (Address 0x0A): 2 (Stays in OUTPUT)
  //   Row 0x0C (user-submit AND loop-ovf both High)
  //   Column 0x01 (Address 0x0D): 2 (Safety catch: prioritize moving to OUTPUT)
  //   Row 0x10 (print-done is High)
  //   Column 0x00 (Address 0x10): 0
  //   Column 0x01 (Address 0x11): 1 (Stays in INFERENCE)
  //   Column 0x02 (Address 0x12): 0  <-- CRITICAL: Printing is done! Moves OUTPUT back to IDLE.
  //   initial master clock = 40 hz
  //   initial printer clock = 2 hz
  //   counter set as 10 bits (max 1024 hz), 
  //   but not necessary.
  //   ------>
  //   contents of StateLUT (hex, n*v repeats v):
  //   0,1,2,0,1,1,2,0,0,2,2,0,0,2,0,0,0,1
  //   reset state?
  //   PRINTER SPEED DIVIDER
  //   if state[1] == 1,
  //   argmax is complete and we're ready to output.
endmodule
