// Digital circuit weight-bank-8bit-0.dig as structural Verilog
module weight_bank_8bit_0 (
  input  [8:0] loop_cnt_addr,
  output [7:0] class_weight
);

  ROM #(.AddrBits(9), .Bits(4)) low_nibble_rom0 (.A(loop_cnt_addr), .sel(1'b1), .D(class_weight[3:0]));
  ROM #(.AddrBits(9), .Bits(4)) high_nibble_rom0 (.A(loop_cnt_addr), .sel(1'b1), .D(class_weight[7:4]));

  // Notes on the sheet:
  //   contents of low_nibble_rom0 (hex, n*v repeats v):
  //   3,c,3,0,2,f,d,2,c,a,5,7,a,8,0,1,4,3,b,2,f,8,6,f,6,b,3,0,4,0,7
  //   ,9,2,6,5,2,d,5,7,2,b,0,a,3,0,3,7,1,d,6,7,3,9,4,a,3,1,b,1,5,0,9
  //   ,3,6,3,b,1,5,6,4,e,6,0,4,2,7,1,7,e,b,8,4,3,a,7,7,5,e,c,1,3,9,9
  //   ,8,5,9,f,a,8,5,5,6,6,c,b,b,c,2,1,4,5,2,8,3,a,b,d,c,c,c,d,9,8,e
  //   ,d,0,0,8,2,9,2,9,2,7,8,5,5,b,7,a,b,2,8,0,a,e,5,1,d,1,5,f,d,4,a
  //   ,c,2,d,6,3,9,3,5,f,d,7,c,5,e,9,0,e,4,2,5,6,b,c,9,9,b,0,4,6,7,8
  //   ,4,d,8,8,4,4,1,3,d,a,6,7,c,1,d,1,5,6,a,b,1,a,3,8,7,7,9,e,4,9,0
  //   ,f,a,3,8,b,9,f,5,2,2,d,8,7,3,2,5,8,2,1,f,8,a,9,d,6,1,c,0,5,9,c
  //   ,5,8,6,f,2,d,b,b,d,e,1
  //   contents of high_nibble_rom0 (hex, n*v repeats v):
  //   d,e,d,d,c,b,d,c,b,e,a,b,4*c,d,c,b,d,d,c,d,9,d,b,a,b,e,c,c,d,b,b,b
  //   ,a,a,d,b,e,a,d,a,d,a,a,b,b,b,c,d,a,c,b,d,c,c,b,c,b,c,b,c,b,b,c
  //   ,a,c,b,e,a,b,b,c,a,9,b,c,9,b,a,a,5*b,c,a,c,a,a,b,a,a,a,9,4*b,a
  //   ,b,a,b,c,b,c,b,d,a,e,b,c,a,a,a,c,9,b,9,4*a,d,b,b,b,c,a,b,b,a,a
  //   ,b,c,a,b,a,4*b,a,a,a,c,a,b,d,9,a,c,a,b,c,a,b,a,a,b,a,8,a,a,9,a,a,a
  //   ,b,b,a,b,a,a,b,a,a,a,b,a,b,b,c,a,a,b,c,b,9,b,a,a,a,9,8,a,a,b,9
  //   ,b,a,9,c,a,9,a,a,9,b,a,a,9,b,9,a,9,5*a,9,9,a,b,9,9,9,a,b,a,a,b
  //   ,a,9,b,9,9,9,a,a,9,a,a,9,9,b,a,9,9,b,9,9,9,a,c,f
endmodule
