// Digital circuit weight-bank-8bit-1.dig as structural Verilog
module weight_bank_8bit_1 (
  input  [8:0] loop_cnt_addr,
  output [7:0] class_weight
);

  ROM #(.AddrBits(9), .Bits(4)) low_nibble_rom1 (.A(loop_cnt_addr), .sel(1'b1), .D(class_weight[3:0]));
  ROM #(.AddrBits(9), .Bits(4)) high_nibble_rom1 (.A(loop_cnt_addr), .sel(1'b1), .D(class_weight[7:4]));

  // Notes on the sheet:
  //   contents of low_nibble_rom1 (hex, n*v repeats v):
  //   6,b,4,1,6,1,f,5,8,0,e,0,b,5,7,4,d,1,6,6,b,1,e,d,f,d,b,a,b,8,a
  //   ,f,8,d,b,b,8,d,7,f,3,f,4,e,b,f,c,4,d,2,6,9,b,6,a,3,9,1,8,c,6,c
  //   ,9,9,f,a,7,4,5,2,1,c,5,1,b,1,7,d,a,1,0,e,9,d,1,7,f,0,e,e,e,9,0
  //   ,7,0,1,f,5,f,f,6,4,b,f,b,8,c,c,a,8,2,5,c,0,4,f,8,3,d,4,3,2,5,7
  //   ,0,e,2,0,0,b,6,4,6,1,f,e,3,8,d,d,2,1,2,5,0,a,5,5,d,9,3,e,2,4,8
  //   ,a,3,5,0,9,c,8,8,7,5,f,9,d,f,d,d,8,3,b,6,9,1,4,6,d,0,d,f,a,6,1
  //   ,d,2,6,c,a,f,5,4,3,6,4,4,0,c,5,9,a,4,5,5,7,6,3,b,7,f,5,0,7,1,8
  //   ,4,7,1,2,1,b,3,8,b,b,e,e,1,2,9,b,9,7,f,0,5,5,9,4,d,9,f,3,d,4,3
  //   ,d,4,f,b,3,3,3,d,0,1,e
  //   contents of high_nibble_rom1 (hex, n*v repeats v):
  //   d,e,d,c,c,c,d,e,b,e,9,b,c,b,c,b,c,b,a,c,d,c,c,9,c,b,9,b,d,b,c,c
  //   ,a,a,a,9,a,d,a,d,a,d,a,c,9,9,a,b,a,c,d,a,c,a,c,c,5*b,a,b,a,a,c
  //   ,9,c,b,e,a,b,a,c,9,9,b,b,a,b,a,9,a,a,b,c,a,d,9,b,9,a,c,a,a,a,9
  //   ,b,a,a,b,9,a,9,b,c,b,b,a,d,a,f,b,c,a,9,a,c,9,b,9,4*a,b,a,b,a,c
  //   ,a,b,b,a,9,a,c,9,a,9,b,b,e,b,a,a,a,b,a,a,d,8,a,b,a,b,c,a,b,9,a,a
  //   ,9,8,a,6*9,b,a,a,a,9,b,a,9,9,c,9,a,b,b,a,9,b,c,a,8,a,9,a,a,8,8
  //   ,a,b,a,9,a,9,8,d,a,8,9,9,9,b,9,a,9,a,8,9,9,4*a,9,9,8,9,a,9,8,9
  //   ,a,a,a,9,a,8,9,b,9,8,9,9,9,8,9,9,8,9,a,9,8,9,a,9,9,8,0,c,e
endmodule
