// Digital circuit weight-bank-8bit-2.dig as structural Verilog
module weight_bank_8bit_2 (
  input  [8:0] loop_cnt_addr,
  output [7:0] class_weight
);

  ROM #(.AddrBits(9), .Bits(4)) low_nibble_rom2 (.A(loop_cnt_addr), .sel(1'b1), .D(class_weight[3:0]));
  ROM #(.AddrBits(9), .Bits(4)) high_nibble_rom2 (.A(loop_cnt_addr), .sel(1'b1), .D(class_weight[7:4]));

  // Notes on the sheet:
  //   contents of low_nibble_rom2 (hex, n*v repeats v):
  //   f,b,9,a,4,e,7,6,5,7,4,e,8,d,7,b,2,1,d,7,2,2,3,f,2,a,1,8,1,c,2
  //   ,e,c,c,c,0,4,2,6,7,6,0,6,2,8,3,2,d,1,4,e,0,7,f,1,c,f,d,e,4,5,4
  //   ,8,2,c,f,2,4,0,4,a,2,8,a,d,a,4,2,0,1,5,2,5,d,c,5,1,1,8,3,e,e,2
  //   ,8,c,a,3,c,f,8,c,3,0,1,e,5,6,f,f,6,b,c,6,1,6,6,8,b,2,5,9,4,3,c
  //   ,d,1,0,1,0,0,9,5,d,0,0,5,7,c,2,0,f,c,c,a,4,9,4,c,e,1,0,d,0,4,8
  //   ,a,a,3,0,1,d,4,c,d,4,4,6,f,2,2,7,a,8,e,3,5,e,2,3,2,3,9,5,6,6,f
  //   ,b,8,b,1,1,5,3,8,c,c,d,b,4,b,7,9,4,f,6,1,f,e,1,b,f,9,9,8,4,c,1
  //   ,c,0,a,0,5,7,1,6,2,9,2,0,5,5,e,d,a,7,2,d,1,3,a,8,d,7,0,4,1,8,f
  //   ,1,f,4,b,d,4,0,2,6,0,3
  //   contents of high_nibble_rom2 (hex, n*v repeats v):
  //   d,e,d,c,c,b,d,c,c,e,a,a,c,b,b,b,d,c,a,c,e,c,d,9,d,b,a,a,e,b,c
  //   ,d,5*a,d,a,e,a,d,a,d,a,a,c,b,c,c,c,a,c,b,d,4*b,c,c,4*b,c,a,c,b
  //   ,e,a,b,a,c,9,9,b,b,b,c,a,a,b,a,b,b,b,d,a,b,9,a,c,4*a,b,a,b,a,a
  //   ,b,a,b,c,c,b,a,d,9,e,b,c,a,a,a,c,a,b,9,4*a,c,b,c,b,d,a,b,b,a,a
  //   ,b,c,9,4*a,b,b,6*a,d,9,a,b,a,b,b,a,b,a,b,a,a,8,a,a,9,9,a,b,a,b
  //   ,5*a,b,a,a,c,9,b,c,c,9,a,c,c,b,9,b,a,a,a,8,8,a,a,a,9,a,a,8,d,d
  //   ,8,9,9,9,b,a,a,9,a,8,9,9,b,5*a,9,a,a,a,9,9,5*a,9,8,b,9,8,9,9,a
  //   ,9,9,a,8,9,b,9,9,9,a,9,9,9,e,c,f
endmodule
