// Digital circuit weight-bank-8bit-3.dig as structural Verilog
module weight_bank_8bit_3 (
  input  [8:0] loop_cnt_addr,
  output [7:0] class_weight
);

  ROM #(.AddrBits(9), .Bits(4)) low_nibble_rom3 (.A(loop_cnt_addr), .sel(1'b1), .D(class_weight[3:0]));
  ROM #(.AddrBits(9), .Bits(4)) high_nibble_rom3 (.A(loop_cnt_addr), .sel(1'b1), .D(class_weight[7:4]));

  // Notes on the sheet:
  //   contents of low_nibble_rom3 (hex, n*v repeats v):
  //   5,d,1,c,f,7,c,8,2,c,2,2,4,e,c,0,7,e,d,7,4,0,7,8,5,1,4,7,e,9,c
  //   ,d,7,e,a,8,6,5,b,2,a,b,9,4,4,3,d,a,e,6,8,d,5,2,9,b,d,2,1,a,a,8
  //   ,6,1,4,e,6,6,1,1,6,3,5,4,3,c,c,0,3,9,1,e,f,7,3,3,0,d,f,7,f,1,a
  //   ,6,5,4,c,3,d,9,4,1,a,f,4,8,c,8,0,6,6,b,e,e,1,2,b,3,e,f,8,8,e,a
  //   ,d,0,a,8,4,a,4,1,b,7,f,e,0,b,6,c,6,5,a,0,5,a,1,d,8,2,a,6,b,6,0
  //   ,d,8,f,b,0,6,7,a,4,1,2,4,e,8,6,a,a,6,5,f,4,3,3,e,6,e,1,8,2,3,0
  //   ,2,7,5,1,3,5,f,5,7,1,a,3,0,a,4,9,5,e,e,f,c,1,3,3,2,e,7,5,d,1,a
  //   ,2,4,1,1,3,0,d,3,8,a,b,0,6,1,4,8,6,8,c,2,a,f,2,3,2,f,1,9,b,4,d
  //   ,f,d,0,1,b,3,0,8,3,0,1
  //   contents of high_nibble_rom3 (hex, n*v repeats v):
  //   d,e,d,c,b,b,d,c,c,e,a,b,c,c,b,c,d,b,c,d,e,d,d,9,d,c,9,a,d,b,c
  //   ,d,a,a,a,9,a,d,a,e,a,c,a,d,a,a,b,a,c,c,d,9,c,b,d,c,b,b,c,b,c,b
  //   ,c,b,b,c,a,c,b,e,a,b,a,c,9,8,b,b,a,c,a,9,a,c,b,b,b,c,9,b,9,a,b
  //   ,a,a,a,9,b,a,b,b,a,a,9,b,c,b,b,b,d,9,e,a,c,a,a,a,d,9,a,9,a,9,a,a
  //   ,d,a,b,b,c,a,b,b,a,9,a,d,9,a,9,b,a,b,b,a,b,4*a,d,9,9,c,a,b,b,9
  //   ,5*a,8,a,a,9,9,a,a,a,b,9,a,9,a,b,a,9,a,b,9,b,c,c,a,b,b,c,b,9,b
  //   ,9,a,b,9,8,a,a,a,9,a,a,8,c,b,8,a,9,9,b,9,a,9,a,9,9,4*a,b,a,9,9,9
  //   ,b,9,9,9,b,4*a,8,9,c,8,9,9,a,6*9,a,a,9,a,a,9,9,9,c,d,f
endmodule
